# Fritzing sketch schematic (saved by Fritzing 1.0.5)
circuit board: 8.46667cm x 5.64444cm

parts:
  esp32 = ESP32 DevKitc V4
  A1 = nrf24l01+palna
  M1 = cc1101 module  # not connected
  OLED1 = OLED 128x64 I2C Monochrome Display VDD-GND
  RE1 = KY-040 Rotary encoder [package="Breakout board"]

nets:
  N1: esp32.IO15, A1.Pin_6
  N2: esp32.IO16, A1.Pin_2
  N3: esp32.IO21, OLED1.SDA
  N4: esp32.IO22, OLED1.SCK
  GND: esp32.GND#18, OLED1.GND, RE1.GND
  3V3: esp32.3V3, A1.Pin_5, RE1.Vcc
  N5: esp32.IO35, RE1.CLK
  N6: esp32.IO32, RE1.DT
  N7: esp32.IO33, RE1.SW
  N8: esp32.IO14, A1.Pin_3
  N9: esp32.IO12, A1.Pin_4
  N10: esp32.GND#32, A1.Pin_1
  N11: esp32.IO13, A1.Pin_7

custom parts:
  ESP32 DevKitc V4: ESP32-DevKitC board with ESP32-WROOM-32 module. ESP32-DevKitC V4 is a small-sized ESP32-based development board produced by Espressif. Most of the pins on the ESP module are broken out to the pin headers on the board. The pins D0, D1, D2, D3, CMD and CLK are used internally for communication between ESP32 and SPI flash memory. They are grouped on both sides near the USB connector. Avoid using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
  cc1101 module: CC1101 rf module.
  OLED 128x64 I2C Monochrome Display VDD-GND: OLED 128x64 I2C Monochrome Display. Note: there are two variants of this part, this one is the VDD GND SCK SDA variant. The other is GND VDD SCK SDA. Make sure you select the part that matches your module as using the incorrect part will probably destroy your module! In addition the mounting holes are marked on silkscreen but not by default drilled. If you want drilled mounting holes, copy a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
  KY-040 Rotary encoder: KY-040 Rotary Encoder with switch on breakout borad from AZ Delivery
